# Fritzing sketch goat2 2 (saved by Fritzing 0.8.7b)
breadboards: 3

parts:
  Composant1 = Arduino Uno (Rev3)
  S1 = Basic Servo
  S2 = Basic Servo
  IR2 = Infrared Proximity Sensor
  Buzz1 = Piezo Speaker
  S1_2 = Toggle Switch [package=THT]
  R1 = Resistor [tolerance=±5% resistance=220 package=THT]
  R2 = Resistor [tolerance=±5% resistance=220 package=THT]
  LED2 = LED - 5mm [color="Yellow (574nm)" package="5 mm [THT]"]
  LED3 = LED - 5mm [color="Green (570nm)" package="5 mm [THT]"]
  R3 = Resistor [tolerance=±5% resistance=220 package=THT]
  R6 = Photocell (LDR) [package=THT]
  R4 = Resistor [tolerance=±5% resistance=220 package=THT]
  R7 = Photocell (LDR) [package=THT]
  R5 = Resistor [tolerance=±5% resistance=220 package=THT]
  IR1 = Infrared Proximity Sensor
  LED1 = smd LED [color="Red (633nm)" package="1206 [SMD]"]
  VCC1 = 4 x AAA Battery Mount

nets:
  N1: Composant1.A0, R6.pin_0, R4.Pin_1
  N2: Composant1.A1, R7.pin_0, R5.Pin_1
  N3: Composant1.A4/SDA, IR1.Vout
  N4: Composant1.A5/SCL, IR2.Vout
  N5: Composant1.D8, Buzz1.pin2
  N6: Composant1.D9_PWM, S1.pulse
  N7: Composant1.D11_PWM/MOSI, S2.pulse
  GND: Composant1.GND, S1.gnd, S2.gnd, IR2.GND, Buzz1.pin1, LED2.cathode, LED3.cathode, R6.pin_1, R7.pin_1, IR1.GND, LED1.cathode, VCC1.-
  N8: Composant1.D7, R3.Pin_1
  VCC: Composant1.5V, S1.vcc, IR2.Vcc, S1_2.COM, IR1.Vcc
  N9: S2.vcc, VCC1.+
  N10: S1_2.L1, R1.Pin_1
  N11: S1_2.L2, R2.Pin_1, R4.Pin_0, R5.Pin_0
  N12: R1.Pin_0, LED1.anode
  N13: R2.Pin_0, LED2.anode
  N14: LED3.anode, R3.Pin_0
